# Fritzing sketch sketch (saved by Fritzing 0.9.4)
circuit board: 10cm x 6cm
breadboards: 1

parts:
  Raspberry_Pi1 = Raspberry Pi 2
  M1 = DC Motor
  IC1 = L293D [package=THT]
  BAT1 = Battery Holders [package=battery-aa]
  M2 = DC Motor

nets:
  N1: Raspberry_Pi1.GND, IC1.0V, BAT1.+
  N2: Raspberry_Pi1.GPIO7, IC1.In_3
  N3: Raspberry_Pi1.GPIO8, IC1.In_4
  N4: Raspberry_Pi1.GPIO24, IC1.In_2
  N5: Raspberry_Pi1.GPIO23, IC1.In_1
  N6: Raspberry_Pi1.5V, IC1.Enable_1, IC1.Enable_2, IC1.+V
  N7: M1.pin_1, IC1.Out_2_(_Controlled_by_Enable_1_)
  N8: M1.pin_2, IC1.Out_1_(_Controlled_by_Enable_1_)
  N9: IC1.+Vmotor, BAT1.-
  N10: IC1.Out_3_(_Controlled_by_Enable_2_), M2.pin_2
  N11: IC1.Out_4_(_Controlled_by_Enable_2_), M2.pin_1
